// Digital circuit main.dig as structural Verilog
module main (
  input  in_1,
  input  in_2,
  input  in_3,
  input  in_4,
  input  in_5,
  input  in_6,
  input  in_7,
  input  in_8
);

  Seven_Seg seven_seg_1 (.a(in_3), .b(in_2), .c(in_8), .d(in_1), .e(in_4), .f(in_5), .g(in_6), .dp(in_7));
endmodule
